# Fritzing sketch ttn_node_rev1_20220620 (saved by Fritzing 0.9.4)
circuit board: 10cm x 12.5cm
perfboards: 1

parts:
  U3 = Adafruit RFM9x LoRa Radio [part_number="Adafruit #3072 and #3073"]
  BAT1 = 18650 battery holder [part_number=LiIon package=battery-18650-kit]
  R1 = Resistor [tolerance=±5% resistance=4.7k part_number=(opt.) power=0.25 package=THT]
  C1 = Electrolytic Capacitor [capacitance=10µF voltage=10V package="100 mil [THT, electrolytic]"]
  J3 = male pin header, 4 pins [form="♂ (male)" part_number="I2C Bus"]
  R2 = Resistor [tolerance=±5% resistance=10k part_number=(opt.) power=0.25 package=THT]
  R3 = Resistor [tolerance=±5% resistance=10k part_number=(opt.) power=0.25 package=THT]
  J4 = male pin header, 7 pins [form="♂ (male)" part_number="SPI Bus"]
  R11 = Resistor [tolerance=±5% resistance=1M power=0.25 package=THT]
  R10 = Resistor [tolerance=±5% resistance=1M power=0.25 package=THT]
  R30 = Resistor [tolerance=±5% resistance=1M power=0.25 package=THT]
  R20 = Resistor [tolerance=±5% resistance=1M power=0.25 package=THT]
  R21 = Resistor [tolerance=±5% resistance=1M power=0.25 package=THT]
  R40 = Resistor [tolerance=±5% resistance=1M power=0.25 package=THT]
  R31 = Resistor [tolerance=±5% resistance=1M power=0.25 package=THT]
  R41 = Resistor [tolerance=±5% resistance=1M power=0.25 package=THT]
  C10 = Ceramic Capacitor [capacitance=100nF voltage=35V package="100 mil [THT, multilayer]"]
  C20 = Ceramic Capacitor [capacitance=100nF voltage=35V package="100 mil [THT, multilayer]"]
  C30 = Ceramic Capacitor [capacitance=100nF voltage=35V package="100 mil [THT, multilayer]"]
  C40 = Ceramic Capacitor [capacitance=100nF voltage=35V package="100 mil [THT, multilayer]"]
  J5 = male pin header, 8 pins [form="♂ (male)"]
  R42 = Resistor [tolerance=±5% resistance=10k part_number=(opt.) power=0.25 package=THT]
  R43 = Resistor [tolerance=±5% resistance=10k part_number=(opt.) power=0.25 package=THT]
  R44 = Resistor [tolerance=±5% resistance=10k part_number=(opt.) power=0.25 package=THT]
  R45 = Resistor [tolerance=±5% resistance=10k part_number=(opt.) power=0.25 package=THT]
  J2 = male pin header, 3 pins [form="♂ (male)" part_number="OneWire Bus"]
  J6 = screw terminal, 3 pins [part_number=Battery]
  U2 = Adafruit BQ24074 Solar-DC-USB Lipo Charger
  U1 = ESP32 FIREBEETLE IOT V3 [part_number=ESP32_FIREBEETLE]
  J7 = Screw terminal - 2 pins [package=THT]
  J8 = male pin header, 4 pins [form="♂ (male)" part_number=GPIO]
  C2 = Electrolytic Capacitor [capacitance=10µF voltage=10V part_number=(opt.) package="100 mil [THT, electrolytic]"]
  F1 = male pin header, 4 pins [form="♂ (male)"]

nets:
  radio_dio1: U3.DIO1, U1.D1/IO16
  radio_dio2: U3.DIO2, U1.LRCK/IO17
  3V3: U3.VIN, R1.Pin_1, C1.+, J3.pin4, R2.Pin_1, R3.Pin_1, J4.pin7, R42.Pin_1, R44.Pin_1, J2.pin2, U1.3V3, J8.pin4, C2.+
  GND: U3.GND, BAT1.-, C1.-, J3.pin1, J4.pin1, R10.Pin_0, R30.Pin_0, R20.Pin_0, R40.Pin_0, C10.0, C20.0, C30.0, C40.0, J5.pin2, J5.pin4, J5.pin6, J5.pin8, R43.Pin_0, R45.Pin_0, J2.pin1, J6.pin1, U2.GND, U1.GND, U1.LIPO-, J7.pin2, J8.pin1, C2.-
  radio_dio0: U3.DIO0, U1.D0/IO4
  sck: U3.SCK, J4.pin2, U1.SCK/IO18
  miso: U3.MISO, J4.pin4, U1.MISO/IO19
  mosi: U3.MOSI, J4.pin3, U1.MOSI/IO23
  radio_cs: U3.CS, R42.Pin_0, R43.Pin_1, U1.BCLK/IO14
  radio_rst: U3.RST, R44.Pin_0, R45.Pin_1, U1.MCLK/IO12
  N1: BAT1.+, J6.pin2, F1.pin3, F1.pin4
  onewire_bus: R1.Pin_0, J2.pin3, U1.IO5/D8
  sda: J3.pin2, R3.Pin_0, U1.SDA/IO21
  scl: J3.pin3, R2.Pin_0, U1.SCL/IO21
  cs0: J4.pin5, U1.IO10/D6
  cs1: J4.pin6, U1.IO13/D7
  A0: R11.Pin_0, R10.Pin_1, C10.1, U1.A0/IO36
  N2: R11.Pin_1, J5.pin1
  A2: R30.Pin_1, R31.Pin_0, C30.1, U1.A2/IO34
  A1: R20.Pin_1, R21.Pin_0, C20.1, U1.A1/IO39
  N3: R21.Pin_1, J5.pin3
  A3: R40.Pin_1, R41.Pin_0, C40.1, U1.A3/IO35
  N4: R31.Pin_1, J5.pin5
  N5: R41.Pin_1, J5.pin7
  N6: J6.pin3, U2.VLIPO, F1.pin1, F1.pin2
  N7: U2.OUT, U1.VCC, U1.LIPO+, J7.pin1
  nCHG: U2.!CHG
  nPGOOD: U2.!PGOOD
  nCE: U2.!CE
  ISET: U2.ISET
  THERM: U2.THERM
  VBUS: U2.VBUS
  D4: U1.IO27/D4, J8.pin2
  D5: U1.IO9/D5, J8.pin3

notes:
  0.1 R1
  TTN Node
  ESP32 LoRaWAN/TTN Node
  Antenna
  LoRaWAN Node
  V1.0
  (C) 06/2022
  M. Prinke
  Batt/Fuse
  B-
  B+
  F_Out
  SolarPwr
  GND
  PWR_
  OneWire
  3V3
  DQ
  I2C
  SDA
  SCL
  SCK
  MOSI
  MISO
  CS0
  CS1
  SPI
  Analog_In
  G
  A0
  A3
  A2
  A1
  GPIO
  D4
  D5
  Out

custom parts:
  Adafruit RFM9x LoRa Radio: Sending data over long distances is like magic, and now you can be a magician with this range of powerful and easy-to-use radio modules. Sure, sometimes you want to talk to a computer (a good time to use WiFi) or perhaps communicate with a Phone (choose Bluetooth Low Energy!) but what if you want to send data very far? Most WiFi, Bluetooth, Zigbee and other wireless chipsets use 2.4GHz, which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
  18650 battery holder: 18650 Battery Holder identical to the dual battery version.
  ESP32 FIREBEETLE IOT V3: DFRobot Firebeetle ESP32 IOT Microcontroller V3, 36-Pin ESP32.
